# Fritzing sketch fritzing (saved by Fritzing 0.9.3b)
breadboards: 1

parts:
  KY-1 = Keyes Relay [package=THT]
  S4 = Magnetic Door Switch [package=reed_switch_plastic]
  WeMos_D1_Mini3 = WeMos D1 Mini

nets:
  N1: KY-1.signal, WeMos_D1_Mini3.D2
  N2: KY-1.power, WeMos_D1_Mini3.5V
  N3: KY-1.ground, S4.1, WeMos_D1_Mini3.G
  N4: S4.2, WeMos_D1_Mini3.D1

notes:
  to existing garage door wall button
  magnetic reed switch

custom parts:
  Keyes Relay: The Keyes 5V relay module is suitable for SCM development, home appliance control. It uses a 5V~12V TIL control signal which can control DC / AC signal.
  WeMos D1 Mini: The D1 mini is a mini wifi board based on ESP-8266EX.
